# Fritzing sketch schematics_base (saved by Fritzing 1.0.7)
breadboards: 1

parts:
  Mod2 = Heltec WiFi Kit 32 V3 [part_number=HTIT-WB32_V3]
  A2 = GT-U8-GPS module
  BMP280_Breakout2 = BMP280 Breakout Board [part_number=BMP280]

nets:
  N1: Mod2.pin_6, A2.Pin_3
  N2: Mod2.pin_16, Mod2.pin_17, A2.Pin_1, BMP280_Breakout2.VCC
  N3: Mod2.pin_18, Mod2.pin_19, A2.Pin_2, BMP280_Breakout2.GND
  N4: Mod2.pin_21, Mod2.pin_22
  N5: Mod2.pin_31, BMP280_Breakout2.SDA
  N6: Mod2.pin_32, BMP280_Breakout2.SCL

custom parts:
  Heltec WiFi Kit 32 V3: The Heltec WiFi Kit 32 (V3) is an IoT development board designed and produced by Heltec Automation and based on the Espressif ESP32 processor module. The board includes WiFi and Bluetooth/BLE functions, as well as a 0.96″ OLED display and a Li-Po battery management system. Links: Heltec WiFi Kit 32 (V3) product page Github
  GT-U8-GPS module: GPS / BDS W/GT-U8 WITH CERAMIC ANTENNA.
  BMP280 Breakout Board: This is a breakout board for the Bosch Sensortec BMP280, "an absolute barometric pressure sensor especially designed for mobile applications." The operation range is 300 to 1100 hPa. Supply voltage is 1.2 to 3.6V. Operating temperature range is -40 to +85 °C.
