# Fritzing sketch schematics_plane (saved by Fritzing 1.0.7)
circuit board: 7.10916cm x 9.37176cm
breadboards: 2

parts:
  U1 = TRANSISTOR_NPN_2 [package=to-92]
  Part2 = I2C level shifter bidirectional
  GPS_Modul = GT-U8-GPS module
  Part4 = HMC5883L Triple-axis Magnetometer [part_number=1746]
  BMP280 = Barometric Pressure Sensor - BMP180 Breakout (GY-68)
  Part3 = InvenSense MPU6050
  SBUS_Empfänger = Dagu DGServo 9g header (male) [package=THT]
  J1 = SBUS Receiver Header [package=THT]
  J2 = SBUS Receiver Header [package=THT]
  J3 = SBUS Receiver Header [package=THT]
  J4 = SBUS Receiver Header [package=THT]
  ADS1115 = ADS1115
  R2 = Resistor [tolerance=±5% resistance=220 power=0.25W package=THT]
  R1 = Resistor [tolerance=±5% resistance=220 power=0.25W package=THT]
  R3 = Resistor [tolerance=±5% resistance=4.7k power=0.25W package=THT]
  R4 = Resistor [tolerance=±5% resistance=4.7k power=0.25W package=THT]
  R5 = Resistor [tolerance=±5% resistance=4.7k power=0.25W package=THT]
  R6 = Resistor [tolerance=±5% resistance=4.7k power=0.25W package=THT]
  Mod1 = Heltec WiFi LoRa 32 V3.2 [part_number=HTIT-WB32LA]
  I2C_Bus = Header 4 [package=jst-4-pth]
  Arduino_Nano = Arduino Nano (Rev3.0)
  Battery_Balancer = Header 4 [package=jst-4-pth]

nets:
  GND: U1.C, Part2.GND, GPS_Modul.Pin_2, Part4.GND, BMP280.GND, Part3.GND, SBUS_Empfänger.gnd, J1.gnd, J2.gnd, J3.gnd, J4.gnd, ADS1115.GND, ADS1115.ADDR, Mod1.pin_18, Mod1.pin_19, I2C_Bus.2, Arduino_Nano.GND, Battery_Balancer.4
  N1: U1.B, R2.Pin_1
  N2: U1.E, R1.Pin_0, Arduino_Nano.D0/RX
  VCC: Part2.LV, GPS_Modul.Pin_1, Part4.VIN, BMP280.VCC, Part3.VCC, ADS1115.VDD, R5.Pin_0, R6.Pin_0, Mod1.pin_16, Mod1.pin_17, I2C_Bus.1
  N3: Part2.LV2, Part4.SCL, BMP280.SCL, Part3.SCL, ADS1115.SCL, R5.Pin_1, Mod1.pin_32, I2C_Bus.3
  N4: Part2.LV1, Part4.SDA, BMP280.SDA, Part3.SDA, ADS1115.SDA, R6.Pin_1, Mod1.pin_31, I2C_Bus.4
  N5: Part2.HV1, R3.Pin_1, Arduino_Nano.A4
  N6: Part2.HV2, R4.Pin_1, Arduino_Nano.A5
  VCC_2: Part2.HV, SBUS_Empfänger.Vcc, J1.Vcc, J2.Vcc, J3.Vcc, J4.Vcc, R1.Pin_1, R3.Pin_0, R4.Pin_0, Mod1.pin_20, Arduino_Nano.5V
  N7: GPS_Modul.Pin_3, Mod1.pin_9
  N8: SBUS_Empfänger.pulse, R2.Pin_0
  N9: J1.signal, Arduino_Nano.D9
  N10: J2.signal, Arduino_Nano.D10
  N11: J3.signal, Arduino_Nano.D11/MOSI
  N12: J4.signal, Arduino_Nano.D12/MISO
  N13: ADS1115.A0, Battery_Balancer.3
  N14: ADS1115.A1, Battery_Balancer.2
  N15: ADS1115.A2, Battery_Balancer.1
  N16: Mod1.pin_21, Mod1.pin_22

custom parts:
  GT-U8-GPS module: GPS / BDS W/GT-U8 WITH CERAMIC ANTENNA.
  ADS1115: ADC ADS1115
  Heltec WiFi LoRa 32 V3.2: The Heltec WiFi LoRa 32 is an IoT development board designed and produced by Heltec Automation and based on the Espressif ESP32-S3FN8 and Semtech SX1262 modules. The board includes WiFi, Bluetooth and LoRa functions, as well as a 0.96″ OLED display and a lithium battery management system. Links: Heltec WiFi LoRa 32 product page Github
