# Fritzing sketch schematics_base (saved by Fritzing 1.0.7)
breadboards: 1

parts:
  GPS_Module = GT-U8-GPS module
  BMP280_Breakout2 = Barometric Pressure Sensor - BMP180 Breakout (GY-68)
  Mod1 = Heltec WiFi LoRa 32 V3.2 [part_number=HTIT-WB32LA]

nets:
  N1: GPS_Module.Pin_1, BMP280_Breakout2.VCC, Mod1.pin_16, Mod1.pin_17
  N2: GPS_Module.Pin_2, BMP280_Breakout2.GND, Mod1.pin_18, Mod1.pin_19
  N3: GPS_Module.Pin_3, Mod1.pin_6
  N4: BMP280_Breakout2.SCL, Mod1.pin_32
  N5: BMP280_Breakout2.SDA, Mod1.pin_31
  N6: Mod1.pin_21, Mod1.pin_22

custom parts:
  GT-U8-GPS module: GPS / BDS W/GT-U8 WITH CERAMIC ANTENNA.
  Heltec WiFi LoRa 32 V3.2: The Heltec WiFi LoRa 32 is an IoT development board designed and produced by Heltec Automation and based on the Espressif ESP32-S3FN8 and Semtech SX1262 modules. The board includes WiFi, Bluetooth and LoRa functions, as well as a 0.96″ OLED display and a lithium battery management system. Links: Heltec WiFi LoRa 32 product page Github
